// Logisim project ex5.circ as structural Verilog: 1 circuit, main circuit main
module main (
  input  A,
  input  B,
  output out_3
);

  wire nor_1_out;

  nor nor_1 (nor_1_out, A, B);
  or or_1 (out_3, A, nor_1_out);
endmodule
